// Logisim project 74xx.circ as structural Verilog: 27 circuits, main circuit 74147
module README (
);


  // Notes on the sheet:
  //   Logisim 74xx series integrated circuits library
  //   Copyright (C) 2015 by Stefan Rothe
  //   This library is licenced under the GNU General Public Licence version 3.
endmodule

module _7400 (
  input  _1A,
  input  _1B,
  input  _2A,
  input  _2B,
  input  _3A,
  input  _3B,
  input  _4A,
  input  _4B,
  output _1Y,
  output _2Y,
  output _3Y,
  output _4Y
);

  nand nand_1 (_1Y, _1A, _1B);
  nand nand_2 (_2Y, _2A, _2B);
  nand nand_3 (_3Y, _3A, _3B);
  nand nand_4 (_4Y, _4A, _4B);
endmodule

module _7402 (
  input  _1A,
  input  _1B,
  input  _2A,
  input  _2B,
  input  _3A,
  input  _3B,
  input  _4A,
  input  _4B,
  output _1Y,
  output _2Y,
  output _3Y,
  output _4Y
);

  nor nor_1 (_1Y, _1A, _1B);
  nor nor_2 (_2Y, _2A, _2B);
  nor nor_3 (_3Y, _3A, _3B);
  nor nor_4 (_4Y, _4A, _4B);
endmodule

module _7404 (
  input  _1A,
  input  _2A,
  input  _3A,
  input  _4A,
  input  _5A,
  input  _6A,
  output _1Y,
  output _2Y,
  output _3Y,
  output _4Y,
  output _5Y,
  output _6Y
);

  not not_1 (_1Y, _1A);
  not not_2 (_2Y, _2A);
  not not_3 (_3Y, _3A);
  not not_4 (_4Y, _4A);
  not not_5 (_5Y, _5A);
  not not_6 (_6Y, _6A);
endmodule

module _7408 (
  input  _1A,
  input  _1B,
  input  _2A,
  input  _2B,
  input  _3A,
  input  _3B,
  input  _4A,
  input  _4B,
  output _1Y,
  output _2Y,
  output _3Y,
  output _4Y
);

  and and_1 (_1Y, _1A, _1B);
  and and_2 (_2Y, _2A, _2B);
  and and_3 (_3Y, _3A, _3B);
  and and_4 (_4Y, _4A, _4B);
endmodule

module _7410 (
  input  _1A,
  input  _1B,
  input  _1C,
  input  _2A,
  input  _2B,
  input  _2C,
  input  _3A,
  input  _3B,
  input  _3C,
  output _1Y,
  output _2Y,
  output _3Y
);

  nand nand_1 (_1Y, _1A, _1B, _1C);
  nand nand_2 (_2Y, _2A, _2B, _2C);
  nand nand_3 (_3Y, _3A, _3B, _3C);
endmodule

module _7411 (
  input  _1A,
  input  _1B,
  input  _1C,
  input  _2A,
  input  _2B,
  input  _2C,
  input  _3A,
  input  _3B,
  input  _3C,
  output _1Y,
  output _2Y,
  output _3Y
);

  and and_1 (_1Y, _1A, _1B, _1C);
  and and_2 (_2Y, _2A, _2C);
  and and_3 (_3Y, _3A, _3C);
endmodule

module _7420 (
  input  _1A,
  input  _1B,
  input  _1C,
  input  _1D,
  input  _2A,
  input  _2B,
  input  _2C,
  input  _2D,
  output _1Y,
  output _2Y
);

  nand nand_1 (_1Y, _1A, _1B, _1C, _1D);
  nand nand_2 (_2Y, _2A, _2B, _2C, _2D);
endmodule

module _7421 (
  input  _1A,
  input  _1B,
  input  _1C,
  input  _1D,
  input  _2A,
  input  _2B,
  input  _2C,
  input  _2D,
  output _1Y,
  output _2Y
);

  and and_1 (_1Y, _1A, _1B, _1C, _1D);
  and and_2 (_2Y, _2A, _2B, _2C, _2D);
endmodule

module _7427 (
  input  _1A,
  input  _1B,
  input  _1C,
  input  _2A,
  input  _2B,
  input  _2C,
  input  _3A,
  input  _3B,
  input  _3C,
  output _1Y,
  output _2Y,
  output _3Y
);

  nor nor_1 (_1Y, _1A, _1B, _1C);
  nor nor_2 (_2Y, _2A, _2B, _2C);
  nor nor_3 (_3Y, _3A, _3B, _3C);
endmodule

module _7432 (
  input  _1A,
  input  _1B,
  input  _2A,
  input  _2B,
  input  _3A,
  input  _3B,
  input  _4A,
  input  _4B,
  output _1Y,
  output _2Y,
  output _3Y,
  output _4Y
);

  or or_1 (_1Y, _1A, _1B);
  or or_2 (_2Y, _2A, _2B);
  or or_3 (_3Y, _3A, _3B);
  or or_4 (_4Y, _4A, _4B);
endmodule

module _7486 (
  input  _1A,
  input  _1B,
  input  _2A,
  input  _2B,
  input  _3A,
  input  _3B,
  input  _4A,
  input  _4B,
  output _1Y,
  output _2Y,
  output _3Y,
  output _4Y
);

  xor xor_1 (_1Y, _1A, _1B);
  xor xor_2 (_2Y, _2A, _2B);
  xor xor_3 (_3Y, _3A, _3B);
  xor xor_4 (_4Y, _4A, _4B);
endmodule

module _74147 (
  input  _1,
  input  _2,
  input  _3,
  input  _4,
  input  _5,
  input  _6,
  input  _7,
  input  _8,
  input  _9,
  output A,
  output B,
  output C,
  output D
);

  wire and_1_out, and_2_out, and_3_out, and_4_out, and_5_out, and_6_out, and_7_out, and_8_out, and_9_out,
       and_10_out, and_11_out, and_12_out, buffer_1_out, nor_1_out, not_1_out, not_2_out, not_3_out,
       not_4_out, not_5_out, not_6_out, not_7_out, not_8_out, not_9_out, not_10_out, not_11_out, not_12_out,
       not_13_out;

  not not_1 (not_1_out, _1);
  not not_2 (not_2_out, _2);
  not not_3 (not_3_out, _3);
  not not_4 (not_4_out, _4);
  not not_5 (not_5_out, _5);
  not not_6 (not_6_out, _6);
  not not_7 (not_7_out, _7);
  not not_8 (not_8_out, _8);
  not not_9 (not_9_out, _9);
  not not_10 (not_10_out, not_2_out);
  not not_11 (not_11_out, not_4_out);
  not not_12 (not_12_out, not_5_out);
  not not_13 (not_13_out, not_6_out);
  nor nor_1 (nor_1_out, not_8_out, not_9_out);
  and and_1 (and_1_out, not_1_out, not_10_out, not_11_out, not_13_out, nor_1_out);
  and and_2 (and_2_out, not_3_out, not_11_out, not_13_out, nor_1_out);
  and and_3 (and_3_out, not_5_out, not_13_out, nor_1_out);
  and and_4 (and_4_out, not_7_out, nor_1_out);
  buf buffer_1 (buffer_1_out, not_9_out);
  and and_5 (and_5_out, not_2_out, not_11_out, not_12_out, nor_1_out);
  and and_6 (and_6_out, not_3_out, not_11_out, not_12_out, nor_1_out);
  and and_7 (and_7_out, not_6_out, nor_1_out);
  and and_8 (and_8_out, not_7_out, nor_1_out);
  and and_9 (and_9_out, not_4_out, nor_1_out);
  and and_10 (and_10_out, not_5_out, nor_1_out);
  and and_11 (and_11_out, not_6_out, nor_1_out);
  and and_12 (and_12_out, not_7_out, nor_1_out);
  nor nor_2 (A, and_1_out, and_2_out, and_3_out, and_4_out, buffer_1_out);
  nor nor_3 (B, and_5_out, and_6_out, and_7_out, and_8_out);
  nor nor_4 (C, and_9_out, and_10_out, and_11_out, and_12_out);
  nor nor_5 (D, not_8_out, not_9_out);
endmodule

module _74157 (
  input  _1A,
  input  _1B,
  input  _2A,
  input  _2B,
  input  _3A,
  input  _3B,
  input  _4A,
  input  _4B,
  input  A_B,
  input  G,
  output _1Y,
  output _2Y,
  output _3Y,
  output _4Y
);

  wire and_1_out, and_2_out, and_3_out, and_4_out, and_5_out, and_6_out, and_7_out, and_8_out, not_1_out,
       not_2_out;

  not not_1 (not_1_out, A_B);
  not not_2 (not_2_out, G);
  and and_1 (and_1_out, _1A, not_1_out, not_2_out);
  and and_2 (and_2_out, _1B, A_B, not_2_out);
  and and_3 (and_3_out, _2A, not_1_out, not_2_out);
  and and_4 (and_4_out, _2B, A_B, not_2_out);
  and and_5 (and_5_out, _3A, not_1_out, not_2_out);
  and and_6 (and_6_out, _3B, A_B, not_2_out);
  and and_7 (and_7_out, _4A, not_1_out, not_2_out);
  and and_8 (and_8_out, _4B, A_B, not_2_out);
  or or_1 (_1Y, and_1_out, and_2_out);
  or or_2 (_2Y, and_3_out, and_4_out);
  or or_3 (_3Y, and_5_out, and_6_out);
  or or_4 (_4Y, and_7_out, and_8_out);
endmodule

module _74161 (
  input  CLK,
  input  MR,
  input  PE,
  input  CEP,
  input  CET,
  input  D0,
  input  D1,
  input  D2,
  input  D3,
  output Q0,
  output Q1,
  output Q2,
  output Q3,
  output TC
);

  wire and_1_out, and_2_out, and_3_out, and_4_out, and_5_out, and_6_out, and_7_out, and_8_out, and_9_out,
       and_10_out, and_11_out, and_12_out, nand_1_out, nand_2_out, nand_3_out, nand_4_out, nand_5_out,
       nand_6_out, nand_7_out, nand_8_out, nand_9_out, nand_10_out, nand_11_out, nand_12_out, nand_13_out,
       nand_14_out, nand_15_out, nand_16_out, nand_17_out, nand_18_out, nand_19_out, nand_20_out,
       nand_21_out, nand_22_out, nand_23_out, nand_24_out, nand_26_out, nand_28_out, nand_30_out,
       nand_32_out, not_1_out, not_2_out, not_3_out, not_4_out, not_5_out, not_6_out, not_7_out, or_1_out,
       or_2_out, or_3_out, or_4_out, xor_1_out, xor_2_out, xor_3_out, xor_4_out;

  not not_1 (not_1_out, CLK);
  not not_2 (not_2_out, MR);
  and and_1 (and_1_out, PE, CEP, CET);
  not not_3 (not_3_out, PE);
  and and_2 (and_2_out, D0, not_3_out);
  and and_3 (and_3_out, Q0, PE);
  and and_4 (and_4_out, D1, not_3_out);
  and and_5 (and_5_out, Q1, PE);
  and and_6 (and_6_out, Q0, and_1_out);
  and and_7 (and_7_out, D2, not_3_out);
  and and_8 (and_8_out, Q2, PE);
  and and_9 (and_9_out, Q1, Q0, and_1_out);
  and and_10 (and_10_out, D3, not_3_out);
  and and_11 (and_11_out, Q3, PE);
  and and_12 (and_12_out, Q2, Q1, Q0, and_1_out);
  xor xor_1 (xor_1_out, and_3_out, and_1_out);
  xor xor_2 (xor_2_out, and_5_out, and_6_out);
  xor xor_3 (xor_3_out, and_8_out, and_9_out);
  xor xor_4 (xor_4_out, and_11_out, and_12_out);
  or or_1 (or_1_out, and_2_out, xor_1_out);
  or or_2 (or_2_out, and_4_out, xor_2_out);
  or or_3 (or_3_out, and_7_out, xor_3_out);
  or or_4 (or_4_out, and_10_out, xor_4_out);
  nand nand_1 (nand_1_out, or_1_out, not_1_out);
  nand nand_2 (nand_2_out, nand_1_out, not_1_out);
  nand nand_3 (nand_3_out, or_2_out, not_1_out);
  nand nand_4 (nand_4_out, nand_3_out, not_1_out);
  nand nand_5 (nand_5_out, or_3_out, not_1_out);
  nand nand_6 (nand_6_out, nand_5_out, not_1_out);
  nand nand_7 (nand_7_out, or_4_out, not_1_out);
  nand nand_8 (nand_8_out, nand_7_out, not_1_out);
  nand nand_9 (nand_9_out, nand_1_out, nand_10_out);
  nand nand_10 (nand_10_out, nand_9_out, nand_2_out, not_2_out);
  not not_4 (not_4_out, not_1_out);
  nand nand_11 (nand_11_out, nand_3_out, nand_12_out);
  nand nand_12 (nand_12_out, nand_11_out, nand_4_out, not_2_out);
  not not_5 (not_5_out, not_1_out);
  nand nand_13 (nand_13_out, nand_5_out, nand_14_out);
  nand nand_14 (nand_14_out, nand_13_out, nand_6_out, not_2_out);
  not not_6 (not_6_out, not_1_out);
  nand nand_15 (nand_15_out, nand_7_out, nand_16_out);
  nand nand_16 (nand_16_out, nand_15_out, nand_8_out, not_2_out);
  not not_7 (not_7_out, not_1_out);
  nand nand_17 (nand_17_out, nand_9_out, not_4_out);
  nand nand_18 (nand_18_out, nand_17_out, not_4_out);
  nand nand_19 (nand_19_out, nand_11_out, not_5_out);
  nand nand_20 (nand_20_out, nand_19_out, not_5_out);
  nand nand_21 (nand_21_out, nand_13_out, not_6_out);
  nand nand_22 (nand_22_out, nand_21_out, not_6_out);
  nand nand_23 (nand_23_out, nand_15_out, not_7_out);
  nand nand_24 (nand_24_out, nand_23_out, not_7_out);
  nand nand_25 (Q0, nand_17_out, nand_26_out);
  nand nand_26 (nand_26_out, Q0, nand_18_out, not_2_out);
  nand nand_27 (Q1, nand_19_out, nand_28_out);
  nand nand_28 (nand_28_out, Q1, nand_20_out, not_2_out);
  nand nand_29 (Q2, nand_21_out, nand_30_out);
  nand nand_30 (nand_30_out, Q2, nand_22_out, not_2_out);
  nand nand_31 (Q3, nand_23_out, nand_32_out);
  nand nand_32 (nand_32_out, Q3, nand_24_out, not_2_out);
  and and_13 (TC, Q3, Q2, Q1, Q0, CET);
endmodule

module _74163 (
  input  CLK,
  input  SR,
  input  PE,
  input  CEP,
  input  CET,
  input  D0,
  input  D1,
  input  D2,
  input  D3,
  output Q0,
  output Q1,
  output Q2,
  output Q3,
  output TC
);

  wire and_1_out, and_2_out, and_3_out, and_4_out, and_5_out, and_6_out, and_7_out, and_8_out, and_9_out,
       and_10_out, and_11_out, and_12_out, and_13_out, nand_1_out, nand_2_out, nand_3_out, nand_4_out,
       nand_5_out, nand_6_out, nand_7_out, nand_8_out, nand_9_out, nand_10_out, nand_11_out, nand_12_out,
       nand_13_out, nand_14_out, nand_15_out, nand_16_out, nand_17_out, nand_18_out, nand_19_out,
       nand_20_out, nand_21_out, nand_22_out, nand_23_out, nand_24_out, nand_26_out, nand_28_out,
       nand_30_out, nand_32_out, not_1_out, not_2_out, not_3_out, not_4_out, not_5_out, not_6_out, not_7_out,
       or_1_out, or_2_out, or_3_out, or_4_out, xor_1_out, xor_2_out, xor_3_out, xor_4_out;

  not not_1 (not_1_out, CLK);
  not not_2 (not_2_out, SR);
  and and_1 (and_1_out, PE, CEP, CET);
  not not_3 (not_3_out, PE);
  and and_2 (and_2_out, D0, not_2_out, not_3_out);
  and and_3 (and_3_out, Q0, not_2_out, PE);
  and and_4 (and_4_out, not_2_out, and_1_out);
  and and_5 (and_5_out, D1, not_2_out, not_3_out);
  and and_6 (and_6_out, Q1, not_2_out, PE);
  and and_7 (and_7_out, Q0, not_2_out, and_1_out);
  and and_8 (and_8_out, D2, not_2_out, not_3_out);
  and and_9 (and_9_out, Q2, not_2_out, PE);
  and and_10 (and_10_out, Q1, Q0, and_1_out, not_2_out);
  and and_11 (and_11_out, D3, not_2_out, not_3_out);
  and and_12 (and_12_out, Q3, not_2_out, PE);
  and and_13 (and_13_out, Q2, Q1, not_2_out, Q0, and_1_out);
  xor xor_1 (xor_1_out, and_3_out, and_4_out);
  xor xor_2 (xor_2_out, and_6_out, and_7_out);
  xor xor_3 (xor_3_out, and_9_out, and_10_out);
  xor xor_4 (xor_4_out, and_12_out, and_13_out);
  or or_1 (or_1_out, and_2_out, xor_1_out);
  or or_2 (or_2_out, and_5_out, xor_2_out);
  or or_3 (or_3_out, and_8_out, xor_3_out);
  or or_4 (or_4_out, and_11_out, xor_4_out);
  nand nand_1 (nand_1_out, or_1_out, not_1_out);
  nand nand_2 (nand_2_out, nand_1_out, not_1_out);
  nand nand_3 (nand_3_out, or_2_out, not_1_out);
  nand nand_4 (nand_4_out, nand_3_out, not_1_out);
  nand nand_5 (nand_5_out, or_3_out, not_1_out);
  nand nand_6 (nand_6_out, nand_5_out, not_1_out);
  nand nand_7 (nand_7_out, or_4_out, not_1_out);
  nand nand_8 (nand_8_out, nand_7_out, not_1_out);
  nand nand_9 (nand_9_out, nand_1_out, nand_10_out);
  nand nand_10 (nand_10_out, nand_9_out, nand_2_out);
  not not_4 (not_4_out, not_1_out);
  nand nand_11 (nand_11_out, nand_3_out, nand_12_out);
  nand nand_12 (nand_12_out, nand_11_out, nand_4_out);
  not not_5 (not_5_out, not_1_out);
  nand nand_13 (nand_13_out, nand_5_out, nand_14_out);
  nand nand_14 (nand_14_out, nand_13_out, nand_6_out);
  not not_6 (not_6_out, not_1_out);
  nand nand_15 (nand_15_out, nand_7_out, nand_16_out);
  nand nand_16 (nand_16_out, nand_15_out, nand_8_out);
  not not_7 (not_7_out, not_1_out);
  nand nand_17 (nand_17_out, nand_9_out, not_4_out);
  nand nand_18 (nand_18_out, nand_17_out, not_4_out);
  nand nand_19 (nand_19_out, nand_11_out, not_5_out);
  nand nand_20 (nand_20_out, nand_19_out, not_5_out);
  nand nand_21 (nand_21_out, nand_13_out, not_6_out);
  nand nand_22 (nand_22_out, nand_21_out, not_6_out);
  nand nand_23 (nand_23_out, nand_15_out, not_7_out);
  nand nand_24 (nand_24_out, nand_23_out, not_7_out);
  nand nand_25 (Q0, nand_17_out, nand_26_out);
  nand nand_26 (nand_26_out, Q0, nand_18_out);
  nand nand_27 (Q1, nand_19_out, nand_28_out);
  nand nand_28 (nand_28_out, Q1, nand_20_out);
  nand nand_29 (Q2, nand_21_out, nand_30_out);
  nand nand_30 (nand_30_out, Q2, nand_22_out);
  nand nand_31 (Q3, nand_23_out, nand_32_out);
  nand nand_32 (nand_32_out, Q3, nand_24_out);
  and and_14 (TC, Q3, Q2, Q1, Q0, CET);
endmodule

module _74181 (
  input  S0,
  input  S1,
  input  S2,
  input  S3,
  input  B3,
  input  A3,
  input  B2,
  input  A2,
  input  B1,
  input  A1,
  input  B0,
  input  A0,
  input  M,
  input  Cn,
  output G,
  output Cn_4,
  output P,
  output F3,
  output F2,
  output A_B,
  output F1,
  output F0
);

  wire and_1_out, and_2_out, and_3_out, and_4_out, and_5_out, and_6_out, and_7_out, and_8_out, and_9_out,
       and_10_out, and_11_out, and_12_out, and_13_out, and_14_out, and_15_out, and_16_out, and_17_out,
       and_18_out, and_19_out, and_20_out, and_21_out, and_22_out, and_23_out, and_24_out, and_25_out,
       and_26_out, and_27_out, and_28_out, buffer_1_out, buffer_2_out, buffer_3_out, buffer_4_out,
       buffer_5_out, nand_1_out, nand_3_out, nor_1_out, nor_2_out, nor_3_out, nor_4_out, nor_5_out,
       nor_6_out, nor_7_out, nor_8_out, nor_10_out, nor_11_out, nor_12_out, not_1_out, not_2_out, not_3_out,
       not_4_out, not_5_out, xor_1_out, xor_2_out, xor_3_out, xor_4_out;

  not not_1 (not_1_out, B3);
  not not_2 (not_2_out, B2);
  not not_3 (not_3_out, B1);
  not not_4 (not_4_out, B0);
  not not_5 (not_5_out, M);
  and and_1 (and_1_out, B3, S0, A3);
  and and_2 (and_2_out, A3, S1, not_1_out);
  and and_3 (and_3_out, not_1_out, S2);
  and and_4 (and_4_out, S3, B3);
  buf buffer_1 (buffer_1_out, A3);
  and and_5 (and_5_out, B2, S0, A2);
  and and_6 (and_6_out, A2, S1, not_2_out);
  and and_7 (and_7_out, not_2_out, S2);
  and and_8 (and_8_out, S3, B2);
  buf buffer_2 (buffer_2_out, A2);
  and and_9 (and_9_out, B1, S0, A1);
  and and_10 (and_10_out, A1, S1, not_3_out);
  and and_11 (and_11_out, not_3_out, S2);
  and and_12 (and_12_out, S3, B1);
  buf buffer_3 (buffer_3_out, A1);
  and and_13 (and_13_out, B0, S0, A0);
  and and_14 (and_14_out, A0, S1, not_4_out);
  and and_15 (and_15_out, not_4_out, S2);
  and and_16 (and_16_out, S3, B0);
  buf buffer_4 (buffer_4_out, A0);
  nor nor_1 (nor_1_out, and_1_out, and_2_out);
  nor nor_2 (nor_2_out, and_3_out, and_4_out, buffer_1_out);
  nor nor_3 (nor_3_out, and_5_out, and_6_out);
  nor nor_4 (nor_4_out, and_7_out, and_8_out, buffer_2_out);
  nor nor_5 (nor_5_out, and_9_out, and_10_out);
  nor nor_6 (nor_6_out, and_11_out, and_12_out, buffer_3_out);
  nor nor_7 (nor_7_out, and_13_out, and_14_out);
  nor nor_8 (nor_8_out, and_15_out, and_16_out, buffer_4_out);
  xor xor_1 (xor_1_out, nor_1_out, nor_2_out);
  xor xor_2 (xor_2_out, nor_3_out, nor_4_out);
  xor xor_3 (xor_3_out, nor_5_out, nor_6_out);
  xor xor_4 (xor_4_out, nor_7_out, nor_8_out);
  buf buffer_5 (buffer_5_out, nor_2_out);
  and and_17 (and_17_out, nor_1_out, nor_4_out);
  and and_18 (and_18_out, nor_1_out, nor_3_out, nor_6_out);
  and and_19 (and_19_out, nor_1_out, nor_3_out, nor_5_out, nor_8_out);
  nand nand_1 (nand_1_out, nor_1_out, nor_3_out, nor_5_out, nor_7_out, Cn);
  nand nand_2 (P, nor_1_out, nor_3_out, nor_5_out, nor_7_out);
  and and_20 (and_20_out, Cn, nor_7_out, nor_5_out, nor_3_out, not_5_out);
  and and_21 (and_21_out, nor_5_out, nor_3_out, nor_8_out, not_5_out);
  and and_22 (and_22_out, nor_3_out, nor_6_out, not_5_out);
  and and_23 (and_23_out, nor_4_out, not_5_out);
  and and_24 (and_24_out, Cn, nor_7_out, nor_5_out, not_5_out);
  and and_25 (and_25_out, nor_5_out, nor_8_out, not_5_out);
  and and_26 (and_26_out, nor_6_out, not_5_out);
  and and_27 (and_27_out, Cn, nor_7_out, not_5_out);
  and and_28 (and_28_out, nor_8_out, not_5_out);
  nand nand_3 (nand_3_out, Cn, not_5_out);
  nor nor_9 (G, buffer_5_out, and_17_out, and_18_out, and_19_out);
  nor nor_10 (nor_10_out, and_20_out, and_21_out, and_22_out, and_23_out);
  nor nor_11 (nor_11_out, and_24_out, and_25_out, and_26_out);
  nor nor_12 (nor_12_out, and_27_out, and_28_out);
  nor nor_13 (Cn_4, G, nand_1_out);
  xor xor_5 (F3, xor_1_out, nor_10_out);
  xor xor_6 (F2, xor_2_out, nor_11_out);
  xor xor_7 (F1, xor_3_out, nor_12_out);
  xor xor_8 (F0, xor_4_out, nand_3_out);
  and and_29 (A_B, F2, F3, F0, F1);
endmodule

module _74244 (
  input  _1A1,
  input  _1A2,
  input  _1A3,
  input  _1A4,
  input  _1OE,
  input  _2A1,
  input  _2A2,
  input  _2A3,
  input  _2A4,
  input  _2OE,
  output _1Y1,
  output _1Y2,
  output _1Y3,
  output _1Y4,
  output _2Y1,
  output _2Y2,
  output _2Y3,
  output _2Y4
);

  wire not_1_out, not_2_out;

  not not_1 (not_1_out, _1OE);
  not not_2 (not_2_out, _2OE);
  assign _1Y1 = not_1_out ? _1A1 : 1'bz;  // Controlled_Buffer controlled_buffer_1
  assign _1Y2 = not_1_out ? _1A2 : 1'bz;  // Controlled_Buffer controlled_buffer_2
  assign _1Y3 = not_1_out ? _1A3 : 1'bz;  // Controlled_Buffer controlled_buffer_3
  assign _1Y4 = not_1_out ? _1A4 : 1'bz;  // Controlled_Buffer controlled_buffer_4
  assign _2Y1 = not_2_out ? _2A1 : 1'bz;  // Controlled_Buffer controlled_buffer_5
  assign _2Y2 = not_2_out ? _2A2 : 1'bz;  // Controlled_Buffer controlled_buffer_6
  assign _2Y3 = not_2_out ? _2A3 : 1'bz;  // Controlled_Buffer controlled_buffer_7
  assign _2Y4 = not_2_out ? _2A4 : 1'bz;  // Controlled_Buffer controlled_buffer_8
endmodule

module _74247 (
  input  LT,
  input  D0,
  input  D1,
  input  D2,
  input  D3,
  input  RBI,
  input  BI,
  output a,
  output b,
  output c,
  output d,
  output e,
  output f,
  output g
);

  wire and_1_out, and_2_out, and_3_out, and_4_out, and_5_out, and_6_out, and_7_out, and_8_out, and_9_out,
       and_10_out, and_11_out, and_12_out, and_13_out, and_14_out, and_15_out, and_16_out, and_17_out,
       buffer_1_out, buffer_2_out, nand_1_out, nand_2_out, nand_3_out, nand_4_out, nand_5_out, nand_6_out,
       nand_7_out, nand_8_out, nor_1_out, nor_2_out, nor_3_out, nor_4_out, nor_5_out, nor_6_out, nor_7_out,
       not_1_out, not_2_out;

  buf buffer_1 (buffer_1_out, LT);
  not not_1 (not_1_out, RBI);
  nand nand_1 (nand_1_out, not_1_out, buffer_1_out, not_2_out, nand_5_out, nand_4_out, nand_3_out);
  nand nand_2 (nand_2_out, nand_1_out, not_2_out);
  nand nand_3 (nand_3_out, D0, buffer_1_out);
  nand nand_4 (nand_4_out, D1, buffer_1_out);
  nand nand_5 (nand_5_out, D2, buffer_1_out);
  not not_2 (not_2_out, D3);
  nand nand_6 (nand_6_out, nand_1_out, nand_5_out);
  nand nand_7 (nand_7_out, nand_1_out, nand_4_out);
  nand nand_8 (nand_8_out, nand_1_out, nand_3_out);
  and and_1 (and_1_out, nand_7_out, nand_2_out);
  and and_2 (and_2_out, nand_3_out, nand_4_out, nand_6_out);
  and and_3 (and_3_out, nand_8_out, nand_4_out, nand_5_out, not_2_out);
  and and_4 (and_4_out, nand_7_out, nand_2_out);
  and and_5 (and_5_out, nand_8_out, nand_4_out, nand_6_out);
  and and_6 (and_6_out, nand_3_out, nand_7_out, nand_6_out);
  and and_7 (and_7_out, nand_6_out, nand_2_out);
  and and_8 (and_8_out, nand_3_out, nand_7_out, nand_5_out);
  and and_9 (and_9_out, nand_8_out, nand_4_out, nand_5_out, not_2_out);
  and and_10 (and_10_out, nand_3_out, nand_4_out, nand_6_out);
  and and_11 (and_11_out, nand_8_out, nand_7_out, nand_6_out);
  buf buffer_2 (buffer_2_out, nand_8_out);
  and and_12 (and_12_out, nand_4_out, nand_6_out);
  and and_13 (and_13_out, nand_8_out, nand_7_out);
  and and_14 (and_14_out, nand_7_out, nand_5_out);
  and and_15 (and_15_out, nand_8_out, nand_5_out, not_2_out);
  and and_16 (and_16_out, nand_8_out, nand_7_out, nand_6_out);
  and and_17 (and_17_out, nand_4_out, nand_5_out, not_2_out, buffer_1_out);
  nor nor_1 (nor_1_out, and_1_out, and_2_out, and_3_out);
  nor nor_2 (nor_2_out, and_4_out, and_5_out, and_6_out);
  nor nor_3 (nor_3_out, and_7_out, and_8_out);
  nor nor_4 (nor_4_out, and_9_out, and_10_out, and_11_out);
  nor nor_5 (nor_5_out, buffer_2_out, and_12_out);
  nor nor_6 (nor_6_out, and_13_out, and_14_out, and_15_out);
  nor nor_7 (nor_7_out, and_16_out, and_17_out);
  not not_3 (a, nor_1_out);
  not not_4 (b, nor_2_out);
  not not_5 (c, nor_3_out);
  not not_6 (d, nor_4_out);
  not not_7 (e, nor_5_out);
  not not_8 (f, nor_6_out);
  not not_9 (g, nor_7_out);
endmodule

module _74373 (
  input  OE,
  input  LE,
  input  _1D,
  input  _2D,
  input  _3D,
  input  _4D,
  input  _5D,
  input  _6D,
  input  _7D,
  input  _8D,
  output _1Q,
  output _2Q,
  output _3Q,
  output _4Q,
  output _5Q,
  output _6Q,
  output _7Q,
  output _8Q
);

  wire buffer_1_out, nand_1_out, nand_2_out, nand_3_out, nand_4_out, nand_5_out, nand_6_out, nand_7_out,
       nand_8_out, nand_9_out, nand_10_out, nand_11_out, nand_12_out, nand_13_out, nand_14_out, nand_15_out,
       nand_16_out, nand_17_out, nand_18_out, nand_19_out, nand_20_out, nand_21_out, nand_22_out,
       nand_23_out, nand_24_out, nand_25_out, nand_26_out, nand_27_out, nand_28_out, nand_29_out,
       nand_30_out, nand_31_out, nand_32_out, not_1_out;

  not not_1 (not_1_out, OE);
  buf buffer_1 (buffer_1_out, LE);
  nand nand_1 (nand_1_out, _1D, buffer_1_out);
  nand nand_2 (nand_2_out, nand_1_out, buffer_1_out);
  nand nand_3 (nand_3_out, _2D, buffer_1_out);
  nand nand_4 (nand_4_out, nand_3_out, buffer_1_out);
  nand nand_5 (nand_5_out, _3D, buffer_1_out);
  nand nand_6 (nand_6_out, nand_5_out, buffer_1_out);
  nand nand_7 (nand_7_out, _4D, buffer_1_out);
  nand nand_8 (nand_8_out, nand_7_out, buffer_1_out);
  nand nand_9 (nand_9_out, _5D, buffer_1_out);
  nand nand_10 (nand_10_out, nand_9_out, buffer_1_out);
  nand nand_11 (nand_11_out, _6D, buffer_1_out);
  nand nand_12 (nand_12_out, nand_11_out, buffer_1_out);
  nand nand_13 (nand_13_out, _7D, buffer_1_out);
  nand nand_14 (nand_14_out, nand_13_out, buffer_1_out);
  nand nand_15 (nand_15_out, _8D, buffer_1_out);
  nand nand_16 (nand_16_out, nand_15_out, buffer_1_out);
  nand nand_17 (nand_17_out, nand_1_out, nand_18_out);
  nand nand_18 (nand_18_out, nand_17_out, nand_2_out);
  nand nand_19 (nand_19_out, nand_3_out, nand_20_out);
  nand nand_20 (nand_20_out, nand_19_out, nand_4_out);
  nand nand_21 (nand_21_out, nand_5_out, nand_22_out);
  nand nand_22 (nand_22_out, nand_21_out, nand_6_out);
  nand nand_23 (nand_23_out, nand_7_out, nand_24_out);
  nand nand_24 (nand_24_out, nand_23_out, nand_8_out);
  nand nand_25 (nand_25_out, nand_9_out, nand_26_out);
  nand nand_26 (nand_26_out, nand_25_out, nand_10_out);
  nand nand_27 (nand_27_out, nand_11_out, nand_28_out);
  nand nand_28 (nand_28_out, nand_27_out, nand_12_out);
  nand nand_29 (nand_29_out, nand_13_out, nand_30_out);
  nand nand_30 (nand_30_out, nand_29_out, nand_14_out);
  nand nand_31 (nand_31_out, nand_15_out, nand_32_out);
  nand nand_32 (nand_32_out, nand_31_out, nand_16_out);
  assign _1Q = not_1_out ? nand_17_out : 1'bz;  // Controlled_Buffer controlled_buffer_1
  assign _2Q = not_1_out ? nand_19_out : 1'bz;  // Controlled_Buffer controlled_buffer_2
  assign _3Q = not_1_out ? nand_21_out : 1'bz;  // Controlled_Buffer controlled_buffer_3
  assign _4Q = not_1_out ? nand_23_out : 1'bz;  // Controlled_Buffer controlled_buffer_4
  assign _5Q = not_1_out ? nand_25_out : 1'bz;  // Controlled_Buffer controlled_buffer_5
  assign _6Q = not_1_out ? nand_27_out : 1'bz;  // Controlled_Buffer controlled_buffer_6
  assign _7Q = not_1_out ? nand_29_out : 1'bz;  // Controlled_Buffer controlled_buffer_7
  assign _8Q = not_1_out ? nand_31_out : 1'bz;  // Controlled_Buffer controlled_buffer_8
endmodule

module _74377 (
  input  CLKEN,
  input  CLK,
  input  _1D,
  input  _2D,
  input  _3D,
  input  _4D,
  input  _5D,
  input  _6D,
  input  _7D,
  input  _8D,
  output _1Q,
  output _2Q,
  output _3Q,
  output _4Q,
  output _5Q,
  output _6Q,
  output _7Q,
  output _8Q
);

  wire and_1_out, not_1_out, not_2_out, or_1_out, or_2_out;

  not not_1 (not_1_out, CLKEN);
  not not_2 (not_2_out, CLK);
  or or_1 (or_1_out, not_1_out, or_2_out);
  or or_2 (or_2_out, or_1_out, not_2_out);
  D_Flip_Flop d_ff_1 (.clk(and_1_out), .D(_1D), .Q(_1Q));  // open: Qn, preset, en, reset
  D_Flip_Flop d_ff_2 (.clk(and_1_out), .D(_2D), .Q(_2Q));  // open: Qn, preset, en, reset
  D_Flip_Flop d_ff_3 (.clk(and_1_out), .D(_3D), .Q(_3Q));  // open: Qn, preset, en, reset
  D_Flip_Flop d_ff_4 (.clk(and_1_out), .D(_4D), .Q(_4Q));  // open: Qn, preset, en, reset
  D_Flip_Flop d_ff_5 (.clk(and_1_out), .D(_5D), .Q(_5Q));  // open: Qn, preset, en, reset
  D_Flip_Flop d_ff_6 (.clk(and_1_out), .D(_6D), .Q(_6Q));  // open: Qn, preset, en, reset
  D_Flip_Flop d_ff_7 (.clk(and_1_out), .D(_7D), .Q(_7Q));  // open: Qn, preset, en, reset
  D_Flip_Flop d_ff_8 (.clk(and_1_out), .D(_8D), .Q(_8Q));  // open: Qn, preset, en, reset
  and and_1 (and_1_out, or_1_out, not_2_out);
endmodule

module _74595 (
  input  D,
  input  OE,
  input  LCLK,
  input  SCLK,
  input  RST,
  output QA,
  output QB,
  output QC,
  output QD,
  output QE,
  output QF,
  output QG,
  output QH,
  output SQH
);

  wire d_ff_1_q, d_ff_2_q, d_ff_3_q, d_ff_4_q, d_ff_5_q, d_ff_6_q, d_ff_7_q, d_ff_9_q, d_ff_10_q, d_ff_11_q,
       d_ff_12_q, d_ff_13_q, d_ff_14_q, d_ff_15_q, d_ff_16_q, not_1_out;

  not not_1 (not_1_out, OE);
  D_Flip_Flop d_ff_1 (.clk(SCLK), .D(D), .Q(d_ff_1_q), .reset(RST));  // open: Qn, preset, en
  D_Flip_Flop d_ff_2 (.clk(SCLK), .D(d_ff_1_q), .Q(d_ff_2_q), .reset(RST));  // open: Qn, preset, en
  D_Flip_Flop d_ff_3 (.clk(SCLK), .D(d_ff_2_q), .Q(d_ff_3_q), .reset(RST));  // open: Qn, preset, en
  D_Flip_Flop d_ff_4 (.clk(SCLK), .D(d_ff_3_q), .Q(d_ff_4_q), .reset(RST));  // open: Qn, preset, en
  D_Flip_Flop d_ff_5 (.clk(SCLK), .D(d_ff_4_q), .Q(d_ff_5_q), .reset(RST));  // open: Qn, preset, en
  D_Flip_Flop d_ff_6 (.clk(SCLK), .D(d_ff_5_q), .Q(d_ff_6_q), .reset(RST));  // open: Qn, preset, en
  D_Flip_Flop d_ff_7 (.clk(SCLK), .D(d_ff_6_q), .Q(d_ff_7_q), .reset(RST));  // open: Qn, preset, en
  D_Flip_Flop d_ff_8 (.clk(SCLK), .D(d_ff_7_q), .Q(SQH), .reset(RST));  // open: Qn, preset, en
  D_Flip_Flop d_ff_9 (.clk(LCLK), .D(d_ff_1_q), .Q(d_ff_9_q));  // open: Qn, preset, en, reset
  D_Flip_Flop d_ff_10 (.clk(LCLK), .D(d_ff_2_q), .Q(d_ff_10_q));  // open: Qn, preset, en, reset
  D_Flip_Flop d_ff_11 (.clk(LCLK), .D(d_ff_3_q), .Q(d_ff_11_q));  // open: Qn, preset, en, reset
  D_Flip_Flop d_ff_12 (.clk(LCLK), .D(d_ff_4_q), .Q(d_ff_12_q));  // open: Qn, preset, en, reset
  D_Flip_Flop d_ff_13 (.clk(LCLK), .D(d_ff_5_q), .Q(d_ff_13_q));  // open: Qn, preset, en, reset
  D_Flip_Flop d_ff_14 (.clk(LCLK), .D(d_ff_6_q), .Q(d_ff_14_q));  // open: Qn, preset, en, reset
  D_Flip_Flop d_ff_15 (.clk(LCLK), .D(d_ff_7_q), .Q(d_ff_15_q));  // open: Qn, preset, en, reset
  D_Flip_Flop d_ff_16 (.clk(LCLK), .D(SQH), .Q(d_ff_16_q));  // open: Qn, preset, en, reset
  assign QA = not_1_out ? d_ff_9_q : 1'bz;  // Controlled_Buffer controlled_buffer_1
  assign QB = not_1_out ? d_ff_10_q : 1'bz;  // Controlled_Buffer controlled_buffer_2
  assign QC = not_1_out ? d_ff_11_q : 1'bz;  // Controlled_Buffer controlled_buffer_3
  assign QD = not_1_out ? d_ff_12_q : 1'bz;  // Controlled_Buffer controlled_buffer_4
  assign QE = not_1_out ? d_ff_13_q : 1'bz;  // Controlled_Buffer controlled_buffer_5
  assign QF = not_1_out ? d_ff_14_q : 1'bz;  // Controlled_Buffer controlled_buffer_6
  assign QG = not_1_out ? d_ff_15_q : 1'bz;  // Controlled_Buffer controlled_buffer_7
  assign QH = not_1_out ? d_ff_16_q : 1'bz;  // Controlled_Buffer controlled_buffer_8
endmodule

module _74670 (
  input  RE,
  input  RA,
  input  RB,
  input  WE,
  input  WA,
  input  WB,
  input  D0,
  input  D1,
  input  D2,
  input  D3,
  output Q0,
  output Q1,
  output Q2,
  output Q3
);

  wire and_1_out, and_2_out, and_3_out, and_4_out, and_5_out, and_6_out, and_7_out, and_8_out, and_9_out,
       and_10_out, and_11_out, and_12_out, and_13_out, and_14_out, and_15_out, and_16_out, and_17_out,
       and_18_out, and_19_out, and_20_out, and_21_out, and_22_out, d_ff_1_q, d_ff_2_q, d_ff_3_q, d_ff_4_q,
       d_ff_5_q, d_ff_6_q, d_ff_7_q, d_ff_8_q, d_ff_9_q, d_ff_10_q, d_ff_11_q, d_ff_12_q, d_ff_13_q,
       d_ff_14_q, d_ff_15_q, d_ff_16_q, nor_1_out, nor_2_out, nor_3_out, nor_4_out, not_1_out, not_2_out,
       not_3_out, not_4_out, not_5_out, not_6_out, not_7_out, not_8_out, not_9_out, not_10_out, not_11_out,
       not_12_out, not_13_out, not_14_out;

  not not_1 (not_1_out, RE);
  not not_2 (not_2_out, RA);
  not not_3 (not_3_out, RB);
  not not_4 (not_4_out, WE);
  not not_5 (not_5_out, WA);
  not not_6 (not_6_out, WB);
  and and_1 (and_1_out, not_6_out, and_2_out);
  not not_7 (not_7_out, D0);
  not not_8 (not_8_out, D1);
  not not_9 (not_9_out, D2);
  not not_10 (not_10_out, D3);
  not not_11 (not_11_out, not_6_out);
  and and_2 (and_2_out, not_5_out, not_4_out);
  and and_3 (and_3_out, and_2_out, not_11_out);
  D_Flip_Flop #(.trigger("high")) d_ff_1 (.clk(and_1_out), .D(not_7_out), .Q(d_ff_1_q));  // open: Qn, preset, en, reset
  D_Flip_Flop #(.trigger("high")) d_ff_2 (.clk(and_1_out), .D(not_8_out), .Q(d_ff_2_q));  // open: Qn, preset, en, reset
  D_Flip_Flop #(.trigger("high")) d_ff_3 (.clk(and_1_out), .D(not_9_out), .Q(d_ff_3_q));  // open: Qn, preset, en, reset
  D_Flip_Flop #(.trigger("high")) d_ff_4 (
    .clk(and_1_out), .D(not_10_out), .Q(d_ff_4_q));  // open: Qn, preset, en, reset
  not not_12 (not_12_out, not_5_out);
  and and_4 (and_4_out, not_6_out, and_5_out);
  D_Flip_Flop #(.trigger("high")) d_ff_5 (.clk(and_3_out), .D(not_7_out), .Q(d_ff_5_q));  // open: Qn, preset, en, reset
  D_Flip_Flop #(.trigger("high")) d_ff_6 (.clk(and_3_out), .D(not_8_out), .Q(d_ff_6_q));  // open: Qn, preset, en, reset
  D_Flip_Flop #(.trigger("high")) d_ff_7 (.clk(and_3_out), .D(not_9_out), .Q(d_ff_7_q));  // open: Qn, preset, en, reset
  D_Flip_Flop #(.trigger("high")) d_ff_8 (
    .clk(and_3_out), .D(not_10_out), .Q(d_ff_8_q));  // open: Qn, preset, en, reset
  and and_5 (and_5_out, not_12_out, not_4_out);
  and and_6 (and_6_out, and_5_out, not_11_out);
  D_Flip_Flop #(.trigger("high")) d_ff_9 (.clk(and_4_out), .D(not_7_out), .Q(d_ff_9_q));  // open: Qn, preset, en, reset
  D_Flip_Flop #(.trigger("high")) d_ff_10 (
    .clk(and_4_out), .D(not_8_out), .Q(d_ff_10_q));  // open: Qn, preset, en, reset
  D_Flip_Flop #(.trigger("high")) d_ff_11 (
    .clk(and_4_out), .D(not_9_out), .Q(d_ff_11_q));  // open: Qn, preset, en, reset
  D_Flip_Flop #(.trigger("high")) d_ff_12 (
    .clk(and_4_out), .D(not_10_out), .Q(d_ff_12_q));  // open: Qn, preset, en, reset
  not not_13 (not_13_out, not_3_out);
  D_Flip_Flop #(.trigger("high")) d_ff_13 (
    .clk(and_6_out), .D(not_7_out), .Q(d_ff_13_q));  // open: Qn, preset, en, reset
  D_Flip_Flop #(.trigger("high")) d_ff_14 (
    .clk(and_6_out), .D(not_8_out), .Q(d_ff_14_q));  // open: Qn, preset, en, reset
  D_Flip_Flop #(.trigger("high")) d_ff_15 (
    .clk(and_6_out), .D(not_9_out), .Q(d_ff_15_q));  // open: Qn, preset, en, reset
  D_Flip_Flop #(.trigger("high")) d_ff_16 (
    .clk(and_6_out), .D(not_10_out), .Q(d_ff_16_q));  // open: Qn, preset, en, reset
  not not_14 (not_14_out, not_2_out);
  and and_7 (and_7_out, d_ff_1_q, not_3_out, not_2_out);
  and and_8 (and_8_out, d_ff_5_q, not_3_out, not_14_out);
  and and_9 (and_9_out, d_ff_9_q, not_13_out, not_2_out);
  and and_10 (and_10_out, d_ff_13_q, not_13_out, not_14_out);
  and and_11 (and_11_out, d_ff_2_q, not_3_out, not_2_out);
  and and_12 (and_12_out, d_ff_6_q, not_3_out, not_14_out);
  and and_13 (and_13_out, d_ff_10_q, not_13_out, not_2_out);
  and and_14 (and_14_out, d_ff_14_q, not_13_out, not_14_out);
  and and_15 (and_15_out, d_ff_3_q, not_3_out, not_2_out);
  and and_16 (and_16_out, d_ff_7_q, not_3_out, not_14_out);
  and and_17 (and_17_out, d_ff_11_q, not_13_out, not_2_out);
  and and_18 (and_18_out, d_ff_15_q, not_13_out, not_14_out);
  and and_19 (and_19_out, d_ff_4_q, not_3_out, not_2_out);
  and and_20 (and_20_out, d_ff_8_q, not_3_out, not_14_out);
  and and_21 (and_21_out, d_ff_12_q, not_13_out, not_2_out);
  and and_22 (and_22_out, d_ff_16_q, not_13_out, not_14_out);
  assign Q0 = not_1_out ? nor_1_out : 1'bz;  // Controlled_Buffer controlled_buffer_1
  nor nor_1 (nor_1_out, and_7_out, and_8_out, and_9_out, and_10_out);
  nor nor_2 (nor_2_out, and_11_out, and_12_out, and_13_out, and_14_out);
  assign Q1 = not_1_out ? nor_2_out : 1'bz;  // Controlled_Buffer controlled_buffer_2
  nor nor_3 (nor_3_out, and_15_out, and_16_out, and_17_out, and_18_out);
  assign Q2 = not_1_out ? nor_3_out : 1'bz;  // Controlled_Buffer controlled_buffer_3
  assign Q3 = not_1_out ? nor_4_out : 1'bz;  // Controlled_Buffer controlled_buffer_4
  nor nor_4 (nor_4_out, and_19_out, and_20_out, and_21_out, and_22_out);
endmodule

module _744075 (
  input  _1A,
  input  _1B,
  input  _1C,
  input  _2A,
  input  _2B,
  input  _2C,
  input  _3A,
  input  _3B,
  input  _3C,
  output _1Y,
  output _2Y,
  output _3Y
);

  or or_1 (_1Y, _1A, _1B, _1C);
  or or_2 (_2Y, _2A, _2B, _2C);
  or or_3 (_3Y, _3A, _3B, _3C);
endmodule

module _744078 (
  input  A,
  input  B,
  input  C,
  input  D,
  input  E,
  input  F,
  input  G,
  input  H,
  output Y,
  output X
);

  nor nor_1 (Y, A, B, C, D, E, F, G, H);
  not not_1 (X, Y);
endmodule

module _744511 (
  input  LT,
  input  D0,
  input  D1,
  input  D2,
  input  D3,
  input  LE,
  input  BL,
  output a,
  output b,
  output c,
  output d,
  output e,
  output f,
  output g
);

  wire nand_1_out, nand_2_out, nand_3_out, nand_4_out, nand_5_out, nand_6_out, nand_7_out, nand_8_out,
       nand_9_out, nand_10_out, nand_11_out, nand_12_out, nand_13_out, nand_14_out, nand_15_out, nand_16_out,
       nand_17_out, nand_18_out, nand_19_out, nand_20_out, nand_21_out, nand_22_out, nand_23_out,
       nand_24_out, nand_25_out, nand_26_out, nand_27_out, nand_28_out, nand_29_out, nand_30_out,
       nand_31_out, nand_32_out, nand_33_out, nand_34_out, not_1_out, or_1_out;

  nand nand_1 (nand_1_out, D0, LE);
  nand nand_2 (nand_2_out, nand_1_out, nand_4_out);
  nand nand_3 (nand_3_out, nand_1_out, LE);
  nand nand_4 (nand_4_out, nand_2_out, nand_3_out);
  nand nand_5 (nand_5_out, nand_6_out, nand_7_out);
  nand nand_6 (nand_6_out, D1, LE);
  nand nand_7 (nand_7_out, nand_5_out, nand_8_out);
  nand nand_8 (nand_8_out, nand_6_out, LE);
  nand nand_9 (nand_9_out, nand_10_out, nand_11_out);
  nand nand_10 (nand_10_out, D2, LE);
  nand nand_11 (nand_11_out, nand_9_out, nand_12_out);
  nand nand_12 (nand_12_out, nand_10_out, LE);
  nand nand_13 (nand_13_out, D3, LE);
  nand nand_14 (nand_14_out, nand_13_out, nand_16_out);
  nand nand_15 (nand_15_out, nand_13_out, LE);
  nand nand_16 (nand_16_out, nand_14_out, nand_15_out);
  or or_1 (or_1_out, nand_5_out, nand_9_out);
  nand nand_17 (nand_17_out, nand_9_out, nand_5_out, nand_4_out);
  nand nand_18 (nand_18_out, nand_9_out, nand_2_out, nand_7_out);
  nand nand_19 (nand_19_out, nand_5_out, nand_4_out, nand_11_out);
  nand nand_20 (nand_20_out, nand_2_out, nand_11_out, nand_7_out);
  nand nand_21 (nand_21_out, nand_9_out, nand_7_out, nand_4_out);
  nand nand_22 (nand_22_out, nand_5_out, nand_11_out);
  nand nand_23 (nand_23_out, nand_16_out, nand_11_out, nand_7_out, nand_4_out);
  nand nand_24 (nand_24_out, nand_9_out, nand_5_out, nand_2_out);
  nand nand_25 (nand_25_out, nand_7_out, nand_11_out, nand_16_out, nand_2_out);
  nand nand_26 (nand_26_out, or_1_out, nand_14_out);
  not not_1 (not_1_out, nand_27_out);
  nand nand_27 (nand_27_out, nand_26_out, BL);
  nand nand_28 (nand_28_out, nand_17_out, not_1_out, nand_21_out, nand_25_out);
  nand nand_29 (nand_29_out, nand_18_out, nand_17_out, not_1_out);
  nand nand_30 (nand_30_out, nand_19_out, not_1_out);
  nand nand_31 (nand_31_out, nand_20_out, nand_21_out, not_1_out, nand_24_out);
  nand nand_32 (nand_32_out, nand_21_out, not_1_out, nand_4_out);
  nand nand_33 (nand_33_out, nand_22_out, not_1_out, nand_24_out, nand_25_out);
  nand nand_34 (nand_34_out, nand_23_out, nand_25_out, not_1_out, nand_24_out);
  nand nand_35 (a, nand_28_out, LT);
  nand nand_36 (b, nand_29_out, LT);
  nand nand_37 (c, nand_30_out, LT);
  nand nand_38 (d, nand_31_out, LT);
  nand nand_39 (e, nand_32_out, LT);
  nand nand_40 (f, nand_33_out, LT);
  nand nand_41 (g, nand_34_out, LT);
endmodule

module D_Latch (
);

  wire nand_1_out, nand_2_out, nand_3_out, nand_4_out, nand_5_out, nand_6_out, nand_7_out, nand_8_out,
       not_1_out, undriven, undriven_2;

  nand nand_1 (nand_1_out, undriven, undriven_2);
  nand nand_2 (nand_2_out, nand_1_out, undriven_2);
  not not_1 (not_1_out, undriven_2);
  nand nand_3 (nand_3_out, nand_1_out, nand_4_out);
  nand nand_4 (nand_4_out, nand_3_out, nand_2_out);
  nand nand_5 (nand_5_out, nand_3_out, not_1_out);
  nand nand_6 (nand_6_out, nand_5_out, not_1_out);
  nand nand_7 (nand_7_out, nand_5_out, nand_8_out);
  nand nand_8 (nand_8_out, nand_7_out, nand_6_out);
endmodule
